# Fritzing sketch ESP8266-programmer (saved by Fritzing 0.9.3b)
circuit board: 5cm x 5cm
breadboards: 1

parts:
  J5 = female pin header, 2 pins [form="♀ (female)"]
  J6 = female pin header, 2 pins [form="♀ (female)"]
  J11 = female pin header, 2 pins [form="♀ (female)"]
  J12 = female pin header, 2 pins [form="♀ (female)"]
  RESET = Pushbutton [package="[THT]"]
  R1 = Resistor [tolerance=±5% resistance=3.3k package=THT]
  R2 = Resistor [tolerance=±5% resistance=3.3k package=THT]
  R3 = Resistor [tolerance=±5% resistance=330 package=THT]
  R4 = Resistor [tolerance=±5% resistance=3.3k package=THT]
  R5 = Resistor [tolerance=±5% resistance=3.3k package=THT]
  PROG = Toggle Switch [package=THT]
  C1 = Electrolytic Capacitor [capacitance=0.1mF package="100 mil [THT, electrolytic]"]
  C2 = Electrolytic Capacitor [capacitance=0.1mF package="100 mil [THT, electrolytic]"]
  J13 = female pin header, 2 pins [form="♀ (female)"]
  U2 = ESP8266 WiFi Module [part_number=ESP8266]
  U3 = Voltage Regulator - 3.3V [part_number=LM1117T package="TO220 [THT]"]

nets:
  N1: J5.pin1, C2.+, U3.input_voltage
  N2: J5.pin2, R3.Pin_0
  N3: J6.pin1, J11.pin2, U2.TXD
  GND: J6.pin2, RESET.Pin_3, RESET.Pin_4, PROG.L1, C1.-, C2.-, J13.pin2, U2.GND, U3.GND
  N4: J11.pin1, R5.Pin_1, PROG.COM, U2.GPIO_0
  N5: J12.pin1, R4.Pin_1, U2.GPIO_2
  N6: J12.pin2, R3.Pin_1, U2.RXD
  N7: RESET.Pin_2, R1.Pin_1, U2.RST
  N8: R1.Pin_0, R2.Pin_0, R4.Pin_0, R5.Pin_0, C1.+, J13.pin1, U2.VCC, U3.output_voltage
  N9: R2.Pin_1, U2.CH_PD

notes:
  vin
  rx
  tx
  gnd
  GPIO0
  GPIO1
  GPIO2
  GPIO3
  3.3v
  GND
  N. Whyte
  ESP8266-Breakout
  V1.2016.11
  VCC

custom parts:
  ESP8266 WiFi Module: Generic WiFi Module based on the ESP8266 with onboard PCB antenna and UART communications
  Voltage Regulator - 3.3V: 3.3V DC Voltage Regulator
