# Fritzing sketch Garagev2 (saved by Fritzing 0.9.3b)
circuit board: 5cm x 5cm
breadboards: 1

parts:
  J1 = Camdenboss CTB0158-2 [part_number="CTB0158-1 Vin" package=THT]
  J2 = Camdenboss CTB0158-2 [part_number="CTB0158-2 Vout" package=THT]
  J3 = Camdenboss CTB0158-3 [part_number="CTB0158-3 - Trigger Sense" package=THT]
  C1 = Electrolytic Capacitor [capacitance=10µF package="100 mil [THT, electrolytic]"]
  C2 = Electrolytic Capacitor [capacitance=10µF package="100 mil [THT, electrolytic]"]
  R1 = Resistor [tolerance=±5% resistance=3.3k package=THT]
  R2 = Resistor [tolerance=±5% resistance=3.3k package=THT]
  R3 = Resistor [tolerance=±5% resistance=3.3k package=THT]
  R4 = Resistor [tolerance=±5% resistance=3.3k package=THT]
  R5 = Resistor [tolerance=±5% resistance=3.3k package=THT]
  R6 = Resistor [tolerance=±5% resistance=1k package=THT]
  Q1 = PNP-Transistor [part_number="PNP 2N3906" package="TO92 [THT]"]
  DEBUG = female pin header, 2 pins [form="♀ (female)"]
  U1 = ESP8266 WiFi Module [part_number=ESP8266]
  U2 = Voltage Regulator - 3.3V [part_number=LM1117T package="TO220 [THT]"]

nets:
  GND: J1.pin1, J2.pin1, J3.pin2, C1.-, C2.-, Q1.E, DEBUG.pin1, U1.GND, U2.GND
  N1: J1.pin2, J2.pin2, C1.+, U2.input_voltage
  N2: J3.pin1, Q1.C
  N3: J3.pin3, R3.Pin_1, U1.RXD
  N4: C2.+, R1.Pin_0, R2.Pin_0, R3.Pin_0, R4.Pin_0, R5.Pin_0, U1.VCC, U2.output_voltage
  N5: R1.Pin_1, U1.RST
  N6: R2.Pin_1, U1.CH_PD
  N7: R4.Pin_1, R6.Pin_0, U1.GPIO_2
  N8: R5.Pin_1, U1.GPIO_0
  N9: R6.Pin_1, Q1.B
  N10: DEBUG.pin2, U1.TXD

notes:
  GND
  TX
  SENSE
  TRIGGER
  +V
  Vin
  V2.2016.12
  hc-relay
  N. Whyte

custom parts:
  ESP8266 WiFi Module: Generic WiFi Module based on the ESP8266 with onboard PCB antenna and UART communications
  Voltage Regulator - 3.3V: 3.3V DC Voltage Regulator
